# Fritzing sketch Circuit diagram (saved by Fritzing 0.9.3b)
breadboards: 1

parts:
  Part1 = Arduino Mega 2560 (Rev3)
  Part2 = Arduino Uno (Rev3) - ICSP
  LCD1 = LCD screen
  Matrix_keypad1 = KEYPAD 4x4
  R2 = Trimmer Potentiometer [maximum_resistance=10kΩ package=THT]
  J1 = Piezo Speaker
  R3 = Resistor [tolerance=±5% resistance=220 package=THT]
  Sensore_PIR_HC-SR501 = HC-SR501 Body Sensor Module

nets:
  N1: Part1.A8, Matrix_keypad1.col1
  N2: Part1.A9, Matrix_keypad1.col2
  N3: Part1.A10, Matrix_keypad1.col3
  N4: Part1.A11, Matrix_keypad1.col4
  N5: Part1.A12, Matrix_keypad1.row1
  N6: Part1.A13, Matrix_keypad1.row2
  N7: Part1.A14, Matrix_keypad1.row3
  N8: Part1.A15, Matrix_keypad1.row4
  N9: Part1.D21/SCL, Sensore_PIR_HC-SR501.OUT
  5V: Part1.5V, LCD1.VDD, R2.leg2, R3.Pin_0, Sensore_PIR_HC-SR501.VCC
  GND: Part1.GND, Part2.GND, LCD1.VSS, LCD1.LED-, R2.leg1, J1.pin1, Sensore_PIR_HC-SR501.GND
  N10: Part1.D50, Part2.D12/MISO
  N11: Part1.D51, Part2.D11_PWM/MOSI
  N12: Part1.D52, Part2.D13/SCK
  N13: Part1.D53, Part2.D10_PWM/SS
  N14: Part2.D8, LCD1.RS
  N15: Part2.D9_PWM, J1.pin2
  N16: Part2.D2, LCD1.DB4
  N17: Part2.D3_PWM, LCD1.DB5
  N18: Part2.D4, LCD1.DB6
  N19: Part2.D5_PWM, LCD1.DB7
  N20: Part2.D6_PWM, LCD1.E
  N21: Part2.D7, LCD1.R/W
  N22: LCD1.V0, R2.wiper
  N23: LCD1.LED+, R3.Pin_1

custom parts:
  KEYPAD 4x4: Matrix keypad 16 buttons, 4 rows x 4 columns
  HC-SR501 Body Sensor Module: Pyroelectric Infrared PIR Motion Sensor Detector Module
